// Logisim project ALU.circ as structural Verilog: 22 circuits, main circuit LeftShift32
module ALU32 (
  input  [31:0] A,
  input  [31:0] B,
  input  [4:0] Sa,
  input  [3:0] Op,
  output [31:0] C,
  output V
);

  wire addersubtractor32_1_v, and_2_out, not_2_out;
  wire [31:0] A_t, B_t, C_t, D, E, F, G, H, I, J, multiplexer_1_out, multiplexer_2_out, multiplexer_4_out,
       multiplexer_5_out;

  Shift32 shift32_1 (.Inp(B), .SA(Sa), .OP(Op), .OutP(A_t));
  assign B_t = A ^ B;  // XOR_Gate xor_1, 32 bits wide
  assign C_t = A | B;  // OR_Gate or_1, 32 bits wide
  assign E = A & B;  // AND_Gate and_1, 32 bits wide
  AdderSubtractor32 addersubtractor32_1 (.A(A), .B(B), .OP(Op), .S(F), .V(addersubtractor32_1_v));
  ThirtytwoBitComp thirtytwobitcomp_1 (.A(A), .B(B), .gt(G), .le(H), .eq(I), .ne(J));
  assign D = ~C_t;  // NOT_Gate not_1, 32 bits wide
  not not_2 (not_2_out, Op[3]);
  and and_2 (and_2_out, Op[1], not_2_out);
  Multiplexer #(.select(2), .width(32), .enable("false")) multiplexer_1 (
    .in0(J), .in1(I), .in2(B_t), .in3(D), .out(multiplexer_1_out), .sel(Op[1:0]));
  Multiplexer #(.select(2), .width(32), .enable("false")) multiplexer_2 (
    .in0(A_t), .in1(A_t), .in2(H), .in3(G), .out(multiplexer_2_out), .sel(Op[1:0]));
  Multiplexer #(.enable("false")) multiplexer_3 (.in0(1'b0), .in1(addersubtractor32_1_v), .out(V), .sel(and_2_out));
  Multiplexer #(.select(2), .width(32), .enable("false")) multiplexer_4 (
    .in0(A_t), .in1(A_t), .in2(F), .in3(F), .out(multiplexer_4_out), .sel(Op[1:0]));
  Multiplexer #(.select(2), .width(32), .enable("false")) multiplexer_5 (
    .in0(E), .in1(C_t), .in2(F), .in3(F), .out(multiplexer_5_out), .sel(Op[1:0]));
  Multiplexer #(.select(2), .width(32), .enable("false")) multiplexer_6 (
    .in0(multiplexer_4_out), .in1(multiplexer_5_out), .in2(multiplexer_1_out), .in3(multiplexer_2_out),
    .out(C), .sel(Op[3:2]));

  // Other names for the same wires on the sheet: M[1:0] = Op[1:0]; N[1:0] = Op[3:2]

  // Notes on the sheet:
  //   Check if it is Add or Subtract to output V
  //   1st mux
  //   1st round of mux
  //   2nd mux
  //   3rd mux
  //   4th mux
  //   5th mux
  //   2nd round of Mux
endmodule

module Shift1Bit (
  input  [31:0] Inp,
  input  [3:0] OP,
  output [31:0] OutP
);

  wire [31:31] multiplexer_1_out;

  Multiplexer #(.enable("false")) multiplexer_1 (.in0(1'b0), .in1(Inp[31]), .out(multiplexer_1_out[31]), .sel(OP[0]));
  Multiplexer #(.width(32), .enable("false")) multiplexer_2 (
    .in0({Inp[30:0], 1'b0}), .in1({multiplexer_1_out[31], Inp[31:1]}), .out(OutP), .sel(OP[3]));

  // Notes on the sheet:
  //   Left shift
  //   Right shift
  //   1st Mux
  //   2nd Mux
endmodule

module Shift2Bit (
  input  [31:0] Inp,
  input  [3:0] OP,
  output [31:0] Outp
);

  wire [31:0] shift1bit_1_outp;

  Shift1Bit shift1bit_1 (.Inp(Inp), .OP(OP), .OutP(shift1bit_1_outp));
  Shift1Bit shift1bit_2 (.Inp(shift1bit_1_outp), .OP(OP), .OutP(Outp));
endmodule

module Shift4Bit (
  input  [31:0] Inp,
  input  [3:0] OP,
  output [31:0] OutP
);

  wire [31:0] shift2bit_1_outp;

  Shift2Bit shift2bit_1 (.Inp(Inp), .OP(OP), .Outp(shift2bit_1_outp));
  Shift2Bit shift2bit_2 (.Inp(shift2bit_1_outp), .OP(OP), .Outp(OutP));
endmodule

module Shift8Bit (
  input  [31:0] Inp,
  input  [3:0] Op,
  output [31:0] OutP
);

  wire [31:0] shift4bit_1_outp;

  Shift4Bit shift4bit_1 (.Inp(Inp), .OP(Op), .OutP(shift4bit_1_outp));
  Shift4Bit shift4bit_2 (.Inp(shift4bit_1_outp), .OP(Op), .OutP(OutP));
endmodule

module Shift16Bit (
  input  [31:0] Inp,
  input  [3:0] OP,
  output [31:0] OutP
);

  wire [31:0] shift8bit_1_outp;

  Shift8Bit shift8bit_1 (.Inp(Inp), .Op(OP), .OutP(shift8bit_1_outp));
  Shift8Bit shift8bit_2 (.Inp(shift8bit_1_outp), .Op(OP), .OutP(OutP));
endmodule

module Shift32 (
  input  [31:0] Inp,
  input  [4:0] SA,
  input  [3:0] OP,
  output [31:0] OutP
);

  wire [31:0] multiplexer_1_out, multiplexer_2_out, multiplexer_3_out, multiplexer_4_out, shift1bit_1_outp,
       shift2bit_1_outp, shift4bit_1_outp, shift8bit_1_outp, shift16bit_1_outp;

  Multiplexer #(.width(32), .enable("false")) multiplexer_1 (
    .in0(Inp), .in1(shift1bit_1_outp), .out(multiplexer_1_out), .sel(SA[0]));
  Shift1Bit shift1bit_1 (.Inp(Inp), .OP(OP), .OutP(shift1bit_1_outp));
  Multiplexer #(.width(32), .enable("false")) multiplexer_2 (
    .in0(multiplexer_1_out), .in1(shift2bit_1_outp), .out(multiplexer_2_out), .sel(SA[1]));
  Shift2Bit shift2bit_1 (.Inp(multiplexer_1_out), .OP(OP), .Outp(shift2bit_1_outp));
  Shift4Bit shift4bit_1 (.Inp(multiplexer_2_out), .OP(OP), .OutP(shift4bit_1_outp));
  Multiplexer #(.width(32), .enable("false")) multiplexer_3 (
    .in0(multiplexer_2_out), .in1(shift4bit_1_outp), .out(multiplexer_3_out), .sel(SA[2]));
  Shift8Bit shift8bit_1 (.Inp(multiplexer_3_out), .Op(OP), .OutP(shift8bit_1_outp));
  Multiplexer #(.width(32), .enable("false")) multiplexer_4 (
    .in0(multiplexer_3_out), .in1(shift8bit_1_outp), .out(multiplexer_4_out), .sel(SA[3]));
  Multiplexer #(.width(32), .enable("false")) multiplexer_5 (
    .in0(multiplexer_4_out), .in1(shift16bit_1_outp), .out(OutP), .sel(SA[4]));
  Shift16Bit shift16bit_1 (.Inp(multiplexer_4_out), .OP(OP), .OutP(shift16bit_1_outp));
endmodule

module Add32 (
  input  [31:0] A,
  input  [31:0] B,
  input  Cin,
  output [31:0] C,
  output V
);

  wire sixteenbitadder_1_cout;

  SixteenBitAdder sixteenbitadder_1 (
    .A(A[15:0]), .B(B[15:0]), .Cin(Cin), .S(C[15:0]), .Cout(sixteenbitadder_1_cout));  // open: V
  SixteenBitAdder sixteenbitadder_2 (
    .A(A[31:16]), .B(B[31:16]), .Cin(sixteenbitadder_1_cout), .S(C[31:16]), .V(V));  // open: Cout

  // Other names for the same wires on the sheet: A_t[15:0] = C[15:0]; B_t[15:0] = C[31:16]
endmodule

module FourBitAdder (
  input  [3:0] A,
  input  [3:0] B,
  input  Cin,
  output [3:0] S,
  output Cout,
  output V
);

  wire onebitadder_1_cout, onebitadder_2_cout, onebitadder_3_cout;

  OneBitAdder onebitadder_1 (.Cout(onebitadder_1_cout), .Cin(Cin), .A(A[0]), .B(B[0]), .S(S[0]));
  OneBitAdder onebitadder_2 (.Cout(onebitadder_2_cout), .Cin(onebitadder_1_cout), .A(B[1]), .B(A[1]), .S(S[1]));
  OneBitAdder onebitadder_3 (.Cout(onebitadder_3_cout), .Cin(onebitadder_2_cout), .A(A[2]), .B(B[2]), .S(S[2]));
  OneBitAdder onebitadder_4 (.Cout(Cout), .Cin(onebitadder_3_cout), .A(A[3]), .B(B[3]), .S(S[3]));
  xor xor_1 (V, Cout, onebitadder_3_cout);

  // Other names for the same wires on the sheet: S1 = S[0]; S2 = S[1]; S3 = S[2]; S4 = S[3]
endmodule

module OneBitAdder (
  input  A,
  input  B,
  input  Cin,
  output S,
  output Cout
);

  wire and_1_out, and_2_out, xor_1_out;

  xor xor_1 (xor_1_out, A, B);
  xor xor_2 (S, xor_1_out, Cin);
  and and_1 (and_1_out, xor_1_out, Cin);
  and and_2 (and_2_out, A, B);
  or or_1 (Cout, and_1_out, and_2_out);

  // Notes on the sheet:
  //   S
endmodule

module SixteenBitAdder (
  input  [15:0] A,
  input  [15:0] B,
  input  Cin,
  output [15:0] S,
  output Cout,
  output V
);

  wire fourbitadder_1_cout, fourbitadder_2_cout, fourbitadder_3_cout;

  FourBitAdder fourbitadder_1 (.A(A[3:0]), .B(B[3:0]), .Cin(Cin), .S(S[3:0]), .Cout(fourbitadder_1_cout));  // open: V
  FourBitAdder fourbitadder_2 (
    .A(A[7:4]), .B(B[7:4]), .Cin(fourbitadder_1_cout), .S(S[7:4]), .Cout(fourbitadder_2_cout));  // open: V
  FourBitAdder fourbitadder_3 (
    .A(A[11:8]), .B(B[11:8]), .Cin(fourbitadder_2_cout), .S(S[11:8]), .Cout(fourbitadder_3_cout));  // open: V
  FourBitAdder fourbitadder_4 (.A(A[15:12]), .B(B[15:12]), .Cin(fourbitadder_3_cout), .S(S[15:12]), .Cout(Cout), .V(V));

  // Other names for the same wires on the sheet: A_t[3:0] = S[3:0]; B_t[3:0] = S[7:4]; C[3:0] = S[11:8];
  //   D[3:0] = S[15:12]
endmodule

module AdderSubtractor32 (
  input  [31:0] A,
  input  [31:0] B,
  input  [3:0] OP,
  output [31:0] S,
  output V
);

  wire sixteenbitadder_1_cout;
  wire [15:0] bit_extender_1_out, xor_1_out, xor_2_out;

  assign bit_extender_1_out = {{15{OP[2]}}, OP[2]};  // Bit_Extender bit_extender_1
  assign xor_1_out = bit_extender_1_out ^ B[15:0];  // XOR_Gate xor_1, 16 bits wide
  SixteenBitAdder sixteenbitadder_1 (
    .A(A[15:0]), .B(xor_1_out), .Cin(OP[2]), .S(S[15:0]), .Cout(sixteenbitadder_1_cout));  // open: V
  assign xor_2_out = bit_extender_1_out ^ B[31:16];  // XOR_Gate xor_2, 16 bits wide
  SixteenBitAdder sixteenbitadder_2 (
    .A(A[31:16]), .B(xor_2_out), .Cin(sixteenbitadder_1_cout), .S(S[31:16]), .V(V));  // open: Cout

  // Other names for the same wires on the sheet: A_t[15:0] = S[15:0]; B_t[15:0] = S[31:16]
endmodule

module OneBitComp (
  input  A,
  input  B,
  output gt,
  output eq
);

  xnor xnor_1 (eq, A, B);

  assign gt = A;
endmodule

module fourBitComp (
  input  [3:0] A,
  input  [3:0] B,
  output gt,
  output eq,
  output ms
);

  wire A_t, B_t, C, D, E, F, G;

  OneBitComp onebitcomp_1 (.A(A[0]), .B(B[0]), .gt(E), .eq(A_t));
  OneBitComp onebitcomp_2 (.A(A[1]), .B(B[1]), .gt(F), .eq(B_t));
  OneBitComp onebitcomp_3 (.A(A[2]), .B(B[2]), .gt(G), .eq(C));
  OneBitComp onebitcomp_4 (.A(A[3]), .B(B[3]), .gt(ms), .eq(D));
  or or_1 (gt, E, F, G, ms);
  and and_1 (eq, D, C, B_t, A_t);

  // Other names for the same wires on the sheet: H = ms
endmodule

module SixteenBitcomp (
  input  [15:0] A,
  input  [15:0] B,
  output gt,
  output eq,
  output ms
);

  wire A_t, B_t, C, D, E, F, G, H;

  fourBitComp fourbitcomp_1 (.A(A[3:0]), .B(B[3:0]), .gt(E), .eq(A_t));  // open: ms
  fourBitComp fourbitcomp_2 (.A(A[7:4]), .B(B[7:4]), .gt(F), .eq(B_t));  // open: ms
  fourBitComp fourbitcomp_3 (.A(A[11:8]), .B(B[11:8]), .gt(G), .eq(C));  // open: ms
  fourBitComp fourbitcomp_4 (.A(A[15:12]), .B(B[15:12]), .gt(H), .eq(D), .ms(ms));
  or or_1 (gt, E, F, G, H);
  and and_1 (eq, D, C, B_t, A_t);

  // Other names for the same wires on the sheet: M = ms
endmodule

module ThirtytwoBitComp (
  input  [31:0] A,
  input  [31:0] B,
  output [31:0] gt,
  output [31:0] le,
  output [31:0] eq,
  output [31:0] ne
);

  wire and_1_out, and_2_out, not_1_out, not_2_out, not_3_out, or_1_out, sixteenbitcomp_1_eq,
       sixteenbitcomp_1_gt, sixteenbitcomp_2_eq, sixteenbitcomp_2_gt, sixteenbitcomp_2_ms;

  SixteenBitcomp sixteenbitcomp_1 (
    .A(A[15:0]), .B(B[15:0]), .gt(sixteenbitcomp_1_gt), .eq(sixteenbitcomp_1_eq));  // open: ms
  SixteenBitcomp sixteenbitcomp_2 (
    .A(A[31:16]), .B(B[31:16]), .gt(sixteenbitcomp_2_gt), .eq(sixteenbitcomp_2_eq), .ms(sixteenbitcomp_2_ms));
  or or_1 (or_1_out, sixteenbitcomp_2_gt, sixteenbitcomp_1_gt);
  and and_1 (and_1_out, sixteenbitcomp_1_eq, sixteenbitcomp_2_eq);
  not not_1 (not_1_out, sixteenbitcomp_2_ms);
  assign eq = {{31{1'b0}}, and_1_out};  // Bit_Extender bit_extender_1
  not not_2 (not_2_out, and_1_out);
  and and_2 (and_2_out, or_1_out, not_1_out);
  assign ne = {{31{1'b0}}, not_2_out};  // Bit_Extender bit_extender_2
  not not_3 (not_3_out, and_2_out);
  assign gt = {{31{1'b0}}, and_2_out};  // Bit_Extender bit_extender_3
  assign le = {{31{1'b0}}, not_3_out};  // Bit_Extender bit_extender_4
endmodule

module OneBitShifter (
  input  CIN,
  input  [31:0] Inp,
  output [31:0] Outp
);


  assign Outp = {Inp[30:0], CIN};
endmodule

module TwoBitShifter (
  input  Cin,
  input  [31:0] Inp,
  output [31:0] Outp
);

  wire [31:0] onebitshifter_1_outp;

  OneBitShifter onebitshifter_1 (.CIN(Cin), .Inp(Inp), .Outp(onebitshifter_1_outp));
  OneBitShifter onebitshifter_2 (.CIN(Cin), .Inp(onebitshifter_1_outp), .Outp(Outp));
endmodule

module fourBitShifter (
  input  Cin,
  input  [31:0] Inp,
  output [31:0] OutP
);

  wire [31:0] twobitshifter_1_outp;

  TwoBitShifter twobitshifter_1 (.Cin(Cin), .Inp(Inp), .Outp(twobitshifter_1_outp));
  TwoBitShifter twobitshifter_2 (.Cin(Cin), .Inp(twobitshifter_1_outp), .Outp(OutP));
endmodule

module EightBitShifter (
  input  Cin,
  input  [31:0] Inp,
  output [31:0] Outp
);

  wire [31:0] fourbitshifter_1_outp;

  fourBitShifter fourbitshifter_1 (.Cin(Cin), .Inp(Inp), .OutP(fourbitshifter_1_outp));
  fourBitShifter fourbitshifter_2 (.Cin(Cin), .Inp(fourbitshifter_1_outp), .OutP(Outp));
endmodule

module sixteenBit (
  input  Cin,
  input  [31:0] Inp,
  output [31:0] OutP
);

  wire [31:0] eightbitshifter_1_outp;

  EightBitShifter eightbitshifter_1 (.Cin(Cin), .Inp(Inp), .Outp(eightbitshifter_1_outp));
  EightBitShifter eightbitshifter_2 (.Cin(Cin), .Inp(eightbitshifter_1_outp), .Outp(OutP));
endmodule

module LeftShift32 (
  input  Cin,
  input  [31:0] B,
  input  [4:0] Sa,
  output [31:0] C
);

  wire [31:0] eightbitshifter_1_outp, fourbitshifter_1_outp, multiplexer_1_out, multiplexer_2_out,
       multiplexer_3_out, multiplexer_4_out, onebitshifter_1_outp, sixteenbit_1_outp, twobitshifter_1_outp;

  Multiplexer #(.width(32), .enable("false")) multiplexer_1 (
    .in0(B), .in1(onebitshifter_1_outp), .out(multiplexer_1_out), .sel(Sa[0]));
  OneBitShifter onebitshifter_1 (.CIN(Cin), .Inp(B), .Outp(onebitshifter_1_outp));
  Multiplexer #(.width(32), .enable("false")) multiplexer_2 (
    .in0(multiplexer_1_out), .in1(twobitshifter_1_outp), .out(multiplexer_2_out), .sel(Sa[1]));
  TwoBitShifter twobitshifter_1 (.Cin(Cin), .Inp(multiplexer_1_out), .Outp(twobitshifter_1_outp));
  fourBitShifter fourbitshifter_1 (.Cin(Cin), .Inp(multiplexer_2_out), .OutP(fourbitshifter_1_outp));
  Multiplexer #(.width(32), .enable("false")) multiplexer_3 (
    .in0(multiplexer_2_out), .in1(fourbitshifter_1_outp), .out(multiplexer_3_out), .sel(Sa[2]));
  EightBitShifter eightbitshifter_1 (.Cin(Cin), .Inp(multiplexer_3_out), .Outp(eightbitshifter_1_outp));
  Multiplexer #(.width(32), .enable("false")) multiplexer_4 (
    .in0(multiplexer_3_out), .in1(eightbitshifter_1_outp), .out(multiplexer_4_out), .sel(Sa[3]));
  Multiplexer #(.width(32), .enable("false")) multiplexer_5 (
    .in0(multiplexer_4_out), .in1(sixteenbit_1_outp), .out(C), .sel(Sa[4]));
  sixteenBit sixteenbit_1 (.Cin(Cin), .Inp(multiplexer_4_out), .OutP(sixteenbit_1_outp));
endmodule
